# Fritzing sketch Schaltplan (saved by Fritzing 0.9.2b)
breadboards: 1

parts:
  Raspberry_Pi1 = Raspberry Pi B+
  Bauteil1 = SRF05 Ultrasonic Rangefinder
  R1 = Resistor [tolerance=±5% resistance=330 package=THT]
  R2 = Resistor [tolerance=±5% resistance=470 package=THT]

nets:
  GND: Raspberry_Pi1.GND, Bauteil1.GND, R2.Pin_1
  N1: Raspberry_Pi1.GPIO24, R1.Pin_1, R2.Pin_0
  N2: Raspberry_Pi1.GPIO18, Bauteil1.Trig
  5V: Raspberry_Pi1.5V, Bauteil1.VCC
  N3: Bauteil1.Echo, R1.Pin_0

notes:
  R1 330Ω
  R2 470Ω
  R1
  R2
